# Fritzing sketch CG_scale_schema_ESP8266_OLED_display (saved by Fritzing 1.0.2b)

parts:
  Bauteil3 = HX711 Weighing Sensor Module
  Bauteil5 = HX711 Weighing Sensor Module
  Squix1 = OLED 0.96" 128x64 I2C SSD1306
  Load_Cell1 = Load Cell - Red/white/black/green
  Load_Cell2 = Load Cell - Red/white/black/green
  Load_Cell3 = Load Cell - Red/white/black/green
  Bauteil6 = HX711 Weighing Sensor Module
  U1 = NodeMCU V1.0

nets:
  VCC: Bauteil3.VCC, Bauteil6.VCC
  GND: Bauteil3.GND, Bauteil5.GND, Bauteil6.GND
  N1: Bauteil3.DO/RX, U1.D2
  N2: Bauteil3.CK/TX, U1.D1
  N3: Bauteil3.E+, Load_Cell2.wire1
  N4: Bauteil3.E-, Load_Cell2.wire2
  N5: Bauteil3.A+, Load_Cell2.wire4
  N6: Bauteil3.A-, Load_Cell2.wire3
  N7: Bauteil5.DO/RX, U1.D7
  N8: Bauteil5.CK/TX, U1.D0
  N9: Bauteil5.E+, Load_Cell3.wire1
  N10: Bauteil5.E-, Load_Cell3.wire2
  N11: Bauteil5.A+, Load_Cell3.wire4
  N12: Bauteil5.A-, Load_Cell3.wire3
  VCC_2: Squix1.VCC, U1.3V3
  GND_2: Squix1.GND, U1.GND
  N13: Squix1.SCL, U1.D3
  N14: Squix1.SCA, U1.D4
  N15: Load_Cell1.wire1, Bauteil6.E+
  N16: Load_Cell1.wire2, Bauteil6.E-
  N17: Load_Cell1.wire3, Bauteil6.A-
  N18: Load_Cell1.wire4, Bauteil6.A+
  N19: Bauteil6.DO/RX, U1.D6
  N20: Bauteil6.CK/TX, U1.D5

notes:
  Power supply 5.5V-9.5V
  OLED display

custom parts:
  Load Cell - Red/white/black/green: A rectangle load cell/weighting pressure Sensor with four wires - Red, white, black, green. Normally corresponding with E+, E-, A+, A- respectively.
  NodeMCU V1.0: ESP8266 based NodeMCU
