# Fritzing sketch CG_scale_schema_ESP8266_PCB_Optimise (saved by Fritzing 1.0.2b)
circuit board: 10cm x 6.5cm

parts:
  R1 = Resistor [tolerance=±5% resistance=22k power=0.25W package=THT]
  R2 = Resistor [tolerance=±5% resistance=10k power=0.25W package=THT]
  D1 = Rectifier Diode [part_number=1N4001 package="300 mil [THT]"]
  L7805 = Voltage Regulator [package=to-220-alt]
  D2 = Rectifier Diode [part_number=1N4001 package="300 mil [THT]"]
  PowerIN = female pin header, 3 pins [form="♀ (female)"]
  HX711_IN1 = female pin header, 4 pins [form="♀ (female)"]
  HX711_IN2 = female pin header, 4 pins [form="♀ (female)"]
  Large_8266 = female pin header, 15 pins [form="♀ (female)"]
  8266 = female pin header, 15 pins [form="♀ (female)"]
  HX711_IN3 = female pin header, 4 pins [form="♀ (female)"]
  Load_Cell_1 = HX711 Weighing Sensor Module  # not connected
  Load_Cell_2 = HX711 Weighing Sensor Module  # not connected
  Load_Cell_3 = HX711 Weighing Sensor Module  # not connected
  Small_8266 = female pin header, 15 pins [form="♀ (female)"]
  HX711_OUT3 = female pin header, 6 pins [form="♀ (female)"]
  LoadCell3 = female pin header, 6 pins [form="♀ (female)"]
  Small_8266_2 = NodeMCU V1.0  # not connected
  HX711_OUT2 = female pin header, 6 pins [form="♀ (female)"]
  LoadCell2 = female pin header, 6 pins [form="♀ (female)"]
  HX711_OUT1 = female pin header, 6 pins [form="♀ (female)"]
  LoadCell1 = female pin header, 6 pins [form="♀ (female)"]
  To_LCD = female pin header, 4 pins [form="♀ (female)"]

nets:
  N1: R1.Pin_0, D1.cathode, L7805.IN
  N2: R1.Pin_1, R2.Pin_0, Large_8266.pin15, Small_8266.pin15
  N3: R2.Pin_1, Large_8266.pin2, Small_8266.pin2, To_LCD.pin2
  N4: D1.anode, PowerIN.pin2
  N5: L7805.GND, D2.anode
  N6: L7805.OUT, Large_8266.pin1, Small_8266.pin1
  N7: D2.cathode, PowerIN.pin1, PowerIN.pin3
  N8: HX711_IN1.pin1, 8266.pin9
  N9: HX711_IN1.pin2, 8266.pin14
  N10: HX711_IN1.pin3, 8266.pin15
  N11: HX711_IN1.pin4, HX711_IN2.pin4, 8266.pin1, HX711_IN3.pin4, To_LCD.pin1
  N12: HX711_IN2.pin1, 8266.pin2, HX711_IN3.pin1
  N13: HX711_IN2.pin2, 8266.pin7
  N14: HX711_IN2.pin3, 8266.pin8
  N15: 8266.pin5, HX711_IN3.pin2
  N16: 8266.pin6, HX711_IN3.pin3
  N17: 8266.pin11, To_LCD.pin4
  N18: 8266.pin12, To_LCD.pin3
  N19: HX711_OUT3.pin1, LoadCell3.pin1
  N20: HX711_OUT3.pin2, LoadCell3.pin2
  N21: HX711_OUT3.pin3, LoadCell3.pin3
  N22: HX711_OUT3.pin4, LoadCell3.pin4
  N23: HX711_OUT3.pin5, LoadCell3.pin5
  N24: HX711_OUT3.pin6, LoadCell3.pin6
  N25: HX711_OUT2.pin1, LoadCell2.pin1
  N26: HX711_OUT2.pin2, LoadCell2.pin2
  N27: HX711_OUT2.pin3, LoadCell2.pin3
  N28: HX711_OUT2.pin4, LoadCell2.pin4
  N29: HX711_OUT2.pin5, LoadCell2.pin5
  N30: HX711_OUT2.pin6, LoadCell2.pin6
  N31: HX711_OUT1.pin1, LoadCell1.pin1
  N32: HX711_OUT1.pin2, LoadCell1.pin2
  N33: HX711_OUT1.pin3, LoadCell1.pin3
  N34: HX711_OUT1.pin4, LoadCell1.pin4
  N35: HX711_OUT1.pin5, LoadCell1.pin5
  N36: HX711_OUT1.pin6, LoadCell1.pin6

custom parts:
  NodeMCU V1.0: ESP8266 based NodeMCU
