# Fritzing sketch CG_scale_schema_ESP8266_Mini (saved by Fritzing 1.0.2b)

parts:
  Bauteil3 = HX711 Weighing Sensor Module
  Bauteil5 = HX711 Weighing Sensor Module
  Load_Cell1 = Load Cell - Red/white/black/green
  Load_Cell2 = Load Cell - Red/white/black/green
  Load_Cell3 = Load Cell - Red/white/black/green
  Bauteil6 = HX711 Weighing Sensor Module
  U1 = NodeMCU V1.0

nets:
  VCC: Bauteil3.VCC, Bauteil6.VCC
  GND: Bauteil3.GND, Bauteil5.GND, Bauteil6.GND
  N1: Bauteil3.DO/RX, U1.D2
  N2: Bauteil3.CK/TX, U1.D1
  N3: Bauteil3.E+, Load_Cell2.wire1
  N4: Bauteil3.E-, Load_Cell2.wire2
  N5: Bauteil3.A+, Load_Cell2.wire4
  N6: Bauteil3.A-, Load_Cell2.wire3
  N7: Bauteil5.DO/RX, U1.D7
  N8: Bauteil5.CK/TX, U1.D0
  N9: Bauteil5.E+, Load_Cell3.wire1
  N10: Bauteil5.E-, Load_Cell3.wire2
  N11: Bauteil5.A+, Load_Cell3.wire4
  N12: Bauteil5.A-, Load_Cell3.wire3
  N13: Load_Cell1.wire1, Bauteil6.E+
  N14: Load_Cell1.wire2, Bauteil6.E-
  N15: Load_Cell1.wire3, Bauteil6.A-
  N16: Load_Cell1.wire4, Bauteil6.A+
  N17: Bauteil6.DO/RX, U1.D6
  N18: Bauteil6.CK/TX, U1.D5

notes:
  Power supply 5.5V-9.5V

custom parts:
  Load Cell - Red/white/black/green: A rectangle load cell/weighting pressure Sensor with four wires - Red, white, black, green. Normally corresponding with E+, E-, A+, A- respectively.
  NodeMCU V1.0: ESP8266 based NodeMCU
